# Fritzing sketch SmartSafe (saved by Fritzing 0.9.4)
breadboards: 3

parts:
  Breadboard4 = Breadboard Split Power
  Breadboard5 = Breadboard Split Power
  Teensy_3_1 = Teensy 3.1
  Part1 = 4x4 Keypad [part_number=101207]
  WIZ820io1 = WIZ820io [part_number=WIZ820io]
  J1 = Basic Servo
  J2 = Basic Servo
  OLED_I2C1 = OLED 128x64 I2C Monochrome Display
  MOTOR1 = 28BYJ-48 Stepper Motor
  Grove1 = Grove 4 Digit Display
  X1 = X113647 Stepper Driver Board [part_number=X113647 package=board]
  VCC1 = Battery
  XTAL1 = CRYSTAL - kHz [frequency="32 kHz"]  # not connected
  hc-sr1 = hc-sr04
  LD1 = LD
  R1 = PHOTOCELL [package=photocell]
  R2 = Trimmer Potentiometer [maximum_resistance=10kΩ package=THT]
  GY-1 = GY-61 ADXL335 Angle Sensor [package="SIP (Single Inline) [THT]"]

nets (from the schematic view):
  N1: Breadboard4.pin3Z, Breadboard4.pin21Z, Breadboard4.pin29Z
  N2: Breadboard4.pin4Y, Breadboard4.pin15Y
  N3: Breadboard4.pin17Y, Breadboard4.pin22Y, Breadboard4.pin29Y
  N4: Breadboard5.pin3Y, Breadboard5.pin12Y, Breadboard5.pin15Y
  N5: Breadboard5.pin3Z, Breadboard5.pin11Z, Breadboard5.pin29Z
  GND: Teensy_3_1.GND, WIZ820io1.GND, J2.gnd, OLED_I2C1.GND, X1.GND, VCC1.-, hc-sr1.Trig, LD1.cathode, R2.leg2
  N6: Teensy_3_1.D0, LD1.anode
  N7: Teensy_3_1.D2, Part1.8
  N8: Teensy_3_1.D3, Part1.7
  N9: Teensy_3_1.D4, Part1.6
  N10: Teensy_3_1.D5, Part1.5
  N11: Teensy_3_1.D6, Part1.4
  N12: Teensy_3_1.D7, Part1.3
  N13: Teensy_3_1.D8, Part1.2
  N14: Teensy_3_1.D9, Part1.1
  N15: Teensy_3_1.D10, WIZ820io1.nSS
  N16: Teensy_3_1.D11, WIZ820io1.MOSI
  N17: Teensy_3_1.D12, WIZ820io1.MISO
  N18: Teensy_3_1.VBat, VCC1.+
  N19: Teensy_3_1.3V3#15, WIZ820io1.VIN
  N20: Teensy_3_1.A14/DAC, R2.wiper
  N21: Teensy_3_1.D13, WIZ820io1.SCLK, OLED_I2C1.SCK, Grove1.CLK, GY-1.Z-OUT
  N22: Teensy_3_1.A0/D14, X1.IN1
  N23: Teensy_3_1.A1/D15, X1.IN2
  N24: Teensy_3_1.A2/D16, X1.IN3
  N25: Teensy_3_1.A3/D17, X1.IN4
  N26: Teensy_3_1.A5/D19, OLED_I2C1.SDA, Grove1.DIO
  N27: Teensy_3_1.A6/D20, hc-sr1.Echo
  N28: Teensy_3_1.A8/D22, J2.pulse
  N29: Teensy_3_1.A9/D23, J1.pulse
  N30: Teensy_3_1.Vin, X1.+V
  VCC: J2.vcc, Grove1.VCC
  N31: MOTOR1.BLUE, X1.BLUE
  N32: MOTOR1.PINK, X1.PINK
  N33: MOTOR1.RED, X1.YELLOW
  N34: MOTOR1.ORANGE, X1.ORANGE
  N35: MOTOR1.YELLOW, X1.RED
  N36: R1.P$2, R2.leg1

custom parts:
  Breadboard Split Power: A custom 6 pin per group power supply strip where the top row (ground) is all bussed together and the bottom row (+V) is split in two groups of 12 pins. This version is modified to be a loadable part and was rescaled to be on the standard 1px = 1thou grid with the size set in inches
  4x4 Keypad: Matrix membrane keypad 4x4
  28BYJ-48 Stepper Motor: 28BYJ-48 gear-reduction stepper motor (small)
  X113647 Stepper Driver Board: A common stepper motor driver board based on ULN2003APG darlington array
  LD: A Generic Red Dot Laser Diode Module (~5mW)
  GY-61 ADXL335 Angle Sensor: GY-61 ADXL335 Angle Sensor Module 3-Axis Analog Accelerometer Tilt Angle Board Triaxial Gravity Acceleration
